# Fritzing sketch Schema_Progetto (saved by Fritzing 1.0.6)
breadboards: 1

parts:
  HC-SR04_Sensor_1 = HC-SR04 Ultrasonic Distance Sensor
  U1 = LuaNode32 / ESP32 [part_number=ESP32S-PIN30]
  R1 = 1k Ω Resistor [package=THT]
  R2 = 1k Ω Resistor [package=THT]
  R3 = 1k Ω Resistor [package=THT]

nets:
  VCC: HC-SR04_Sensor_1.VCC, U1.Vin
  N1: HC-SR04_Sensor_1.TRIG, U1.D12
  N2: HC-SR04_Sensor_1.ECHO, R1.Pin_0
  GND: HC-SR04_Sensor_1.GND, U1.GND, R3.Pin_1
  N3: R1.Pin_1, R2.Pin_0
  N4: R2.Pin_1, R3.Pin_0

custom parts:
  LuaNode32 / ESP32: New Image for LuaNode32 DOIT ESP32 DEVKIT V1. Base parts from LuaNode32 / ESP32 ESP32 based LuaNode32 by G.Noorlander DOIT Esp32 DevKit v1 (30 pins long, 11 pins width) by Werner Rothschopf (modified by vanepp Dec 2018)
  1k Ω Resistor: A generic resistor (0.25W)
